// Logisim project Class_Wk5_MUX_DEC.circ as structural Verilog: 4 circuits, main circuit IC5_MUXDEC
module IC5_MUXDEC (
  input  C_in,
  input  A,
  input  B,
  output out_4,
  output out_5,
  output out_6,
  output out_7
);

  MUX_FA mux_fa_1 (.C_in(C_in), .A(A), .B(B), .Sum(out_4), .C_out(out_5));
  MUX_Decoder mux_decoder_1 (.C_in(C_in), .A(A), .B(B), .Sum(out_6), .C_out(out_7));
endmodule

module MUX_FA (
  input  C_in,
  input  A,
  input  B,
  output Sum,
  output C_out
);

  Multiplexer #(.select(3)) multiplexer_1 (
    .in0(1'b0), .in1(1'b0), .in2(1'b0), .in3(1'b1), .in4(1'b0), .in5(1'b1), .in6(1'b1), .in7(1'b1),
    .out(C_out), .sel({B, A, C_in}));
  Multiplexer #(.select(3)) multiplexer_2 (
    .in0(1'b0), .in1(1'b1), .in2(1'b1), .in3(1'b0), .in4(1'b1), .in5(1'b0), .in6(1'b0), .in7(1'b1),
    .out(Sum), .sel({B, A, C_in}));
endmodule

module MUX_Decoder (
  input  C_in,
  input  A,
  input  B,
  output Sum,
  output C_out
);

  wire decoder_1_out3, decoder_1_out5, decoder_1_out6, decoder_1_out7, decoder_2_out1, decoder_2_out2,
       decoder_2_out4, decoder_2_out7;

  Decoder #(.select(3)) decoder_1 (
    .out3(decoder_1_out3), .out5(decoder_1_out5), .out6(decoder_1_out6), .out7(decoder_1_out7),
    .sel({B, A, C_in}));  // open: out0, out1, out2, out4, en
  or or_1 (C_out, decoder_1_out3, decoder_1_out5, decoder_1_out6, decoder_1_out7);
  Decoder #(.select(3)) decoder_2 (
    .out1(decoder_2_out1), .out2(decoder_2_out2), .out4(decoder_2_out4), .out7(decoder_2_out7),
    .sel({B, A, C_in}));  // open: out0, out3, out5, out6, en
  or or_2 (Sum, decoder_2_out1, decoder_2_out2, decoder_2_out4, decoder_2_out7);
endmodule

module Test (
  input  C_in,
  input  A,
  input  B
);

  wire C_out0, C_out1, S, Sum0, Sum1;

  MUX_FA mux_fa_1 (.C_in(C_in), .A(A), .B(B), .Sum(C_out0), .C_out(Sum0));
  MUX_Decoder mux_decoder_1 (.C_in(C_in), .A(A), .B(B), .Sum(C_out1), .C_out(Sum1));
  Multiplexer multiplexer_1 (.in0(C_out0), .in1(Sum0), .sel(S));  // open: out
  Multiplexer multiplexer_2 (.in0(C_out1), .in1(Sum1));  // open: out, sel
endmodule
