// Logisim project Class_Wk7_Mem.circ as structural Verilog: 1 circuit, main circuit main
module main (
  input  Serial_Load,
  input  Serial_In,
  input  Clock,
  input  [3:0] Parallel_In,
  output [3:0] Serial_Out,
  output [3:0] out_6
);

  wire multiplexer_1_out, multiplexer_2_out, multiplexer_3_out, multiplexer_4_out;

  T_Flip_Flop t_ff_1 (.T(multiplexer_1_out), .clk(Clock), .Q(Serial_Out[3]));  // open: Qn, reset, preset
  Multiplexer multiplexer_1 (.in0(Serial_In), .in1(Parallel_In[3]), .out(multiplexer_1_out), .sel(Serial_Load));
  T_Flip_Flop t_ff_2 (.T(multiplexer_2_out), .clk(Clock), .Q(Serial_Out[2]));  // open: Qn, reset, preset
  Multiplexer multiplexer_2 (.in0(Serial_Out[3]), .in1(Parallel_In[2]), .out(multiplexer_2_out), .sel(Serial_Load));
  T_Flip_Flop t_ff_3 (.T(multiplexer_3_out), .clk(Clock), .Q(Serial_Out[1]));  // open: Qn, reset, preset
  Multiplexer multiplexer_3 (.in0(Serial_Out[2]), .in1(Parallel_In[1]), .out(multiplexer_3_out), .sel(Serial_Load));
  Multiplexer multiplexer_4 (.in0(Serial_Out[1]), .in1(Parallel_In[0]), .out(multiplexer_4_out), .sel(Serial_Load));
  T_Flip_Flop t_ff_4 (.T(multiplexer_4_out), .clk(Clock), .Q(Serial_Out[0]));  // open: Qn, reset, preset

  // Other names for the same wires on the sheet: Q0 = out_6[0]; QI = out_6[1]; Q2 = out_6[2]; Q3 = out_6[3];
  //   s = Serial_Load
endmodule
