// Logisim project Lab_7_ENCE2012 - Copy.circ as structural Verilog: 12 circuits, main circuit Seg7_Decoder
module Seg7_Decoder (
  input  i_m3,
  input  i_m2,
  input  i_m1,
  input  i_m0,
  output [7:0] o_seg
);

  wire and_1_out, and_2_out, and_3_out, and_4_out, and_5_out, and_6_out, and_7_out, and_8_out, and_9_out,
       and_10_out, and_11_out, and_12_out, and_13_out, and_14_out, and_15_out, and_16_out, and_17_out,
       and_18_out, and_19_out, and_20_out, and_21_out, and_22_out, and_23_out, not_1_out, not_2_out,
       not_3_out, not_4_out;

  not not_1 (not_1_out, i_m3);
  not not_2 (not_2_out, i_m2);
  not not_3 (not_3_out, i_m1);
  not not_4 (not_4_out, i_m0);
  and and_1 (and_1_out, not_1_out, not_2_out, not_3_out);
  and and_2 (and_2_out, not_1_out, i_m2, i_m1, i_m0);
  and and_3 (and_3_out, i_m3, not_2_out, i_m1);
  and and_4 (and_4_out, not_1_out, not_2_out, i_m0);
  and and_5 (and_5_out, not_1_out, not_2_out, i_m1);
  and and_6 (and_6_out, not_2_out, i_m1, i_m0);
  and and_7 (and_7_out, i_m3, i_m2, not_3_out);
  and and_8 (and_8_out, not_1_out, i_m2, not_3_out);
  and and_9 (and_9_out, i_m3, i_m2, i_m1);
  and and_10 (and_10_out, not_1_out, not_2_out, not_3_out, i_m0);
  and and_11 (and_11_out, not_1_out, i_m2, not_3_out, not_4_out);
  and and_12 (and_12_out, not_1_out, i_m2, i_m1, i_m0);
  and and_13 (and_13_out, i_m3, not_2_out, i_m1, i_m0);
  and and_14 (and_14_out, i_m3, i_m2, i_m1, not_4_out);
  and and_15 (and_15_out, not_1_out, not_2_out, i_m1, not_4_out);
  and and_16 (and_16_out, i_m3, i_m2, not_3_out, not_4_out);
  and and_17 (and_17_out, not_1_out, i_m2, not_3_out, i_m0);
  and and_18 (and_18_out, not_1_out, i_m2, i_m1, not_4_out);
  and and_19 (and_19_out, i_m3, i_m2, i_m1, i_m0);
  and and_20 (and_20_out, not_1_out, not_2_out, not_3_out, i_m0);
  and and_21 (and_21_out, not_1_out, i_m2, not_3_out, not_4_out);
  and and_22 (and_22_out, i_m3, not_2_out, i_m1, i_m0);
  and and_23 (and_23_out, i_m3, i_m2, i_m1, not_4_out);
  or or_1 (o_seg[6], and_1_out, and_2_out, and_3_out);
  or or_2 (o_seg[5], and_4_out, and_5_out, and_6_out, and_7_out);
  or or_3 (o_seg[4], i_m0, and_8_out, and_9_out);
  or or_4 (o_seg[3], and_10_out, and_11_out, and_12_out, and_13_out, and_14_out);
  or or_5 (o_seg[2], and_15_out, and_16_out);
  or or_6 (o_seg[1], and_17_out, and_18_out, and_19_out);
  or or_7 (o_seg[0], and_20_out, and_21_out, and_22_out, and_23_out);

  assign o_seg[7] = 1'b1;
endmodule

module CircuitA (
  input  i2,
  input  i1,
  input  i0,
  output o2,
  output o1,
  output o0
);

  not not_1 (o1, i1);
  and and_1 (o2, i2, i1);

  assign o0 = i0;
endmodule

module myComparator (
  input  v3,
  input  v2,
  input  v1,
  input  v0,
  output z
);

  wire and_1_out, and_2_out;

  and and_1 (and_1_out, v3, v1);
  and and_2 (and_2_out, v3, v2);
  or or_1 (z, and_1_out, and_2_out);
endmodule

module CircuitB (
  input  z,
  output s6,
  output s5,
  output s4,
  output s3,
  output s2,
  output s1,
  output s0
);


  assign s0 = z;
  assign s1 = 1'b0;
  assign s2 = 1'b0;
  assign s3 = z;
  assign s4 = z;
  assign s5 = z;
  assign s6 = 1'b1;
endmodule

module Bin2Hex (
  input  v3,
  input  v2,
  input  v1,
  input  v0,
  output [7:0] HEX1,
  output [7:0] HEX0
);

  wire z;

  myComparator myComparator_1 (.v3(v3), .v2(v2), .v1(v1), .v0(v0), .z(z));
  CircuitB CircuitB_1 (
    .z(z), .s6(HEX1[6]), .s5(HEX1[5]), .s4(HEX1[4]), .s3(HEX1[3]), .s2(HEX1[2]), .s1(HEX1[1]), .s0(HEX1[0]));
  Seg7_Decoder Seg7_Decoder_1 (.i_m3(v3), .i_m2(v2), .i_m1(v1), .i_m0(v0), .o_seg(HEX0));

  assign HEX1[7] = 1'b1;
endmodule

module pedestrian_button (
  input  [3:0] counter,
  input  stopper,
  input  reds,
  input  done,
  output en,
  output stopped
);

  wire d_ff_1_q, d_ff_2_q, or_1_out;

  D_Flip_Flop d_ff_1 (.Q(d_ff_1_q), .preset(stopper), .reset(done));  // open: D, clk, Qn
  or or_1 (or_1_out, counter[0], counter[1], counter[2], counter[3]);
  D_Flip_Flop d_ff_2 (.D(d_ff_1_q), .clk(reds), .Q(d_ff_2_q), .reset(done));  // open: Qn, preset
  and and_1 (en, ~d_ff_2_q, or_1_out);  // AND_Gate

  assign stopped = en;
endmodule

module DownCounter_3 (
  input  en,
  input  clk,
  output [3:0] count
);

  wire and_1_out, and_2_out, and_3_out, and_4_out, t_ff_1_q, t_ff_2_q, t_ff_3_q;

  T_Flip_Flop t_ff_1 (.T(en), .clk(clk), .Q(t_ff_1_q), .Qn(count[0]));  // open: reset, preset
  and and_1 (and_1_out, count[0], count[1], count[2], count[3]);
  and and_2 (and_2_out, en, t_ff_1_q);
  T_Flip_Flop t_ff_2 (.T(and_2_out), .clk(clk), .Q(t_ff_2_q), .Qn(count[1]));  // open: reset, preset
  and and_3 (and_3_out, and_2_out, t_ff_2_q);
  T_Flip_Flop t_ff_3 (.T(and_3_out), .clk(clk), .Q(t_ff_3_q), .Qn(count[2]), .preset(and_1_out));  // open: reset
  and and_4 (and_4_out, and_3_out, t_ff_3_q);
  T_Flip_Flop t_ff_4 (.T(and_4_out), .clk(clk), .Qn(count[3]), .preset(and_1_out));  // open: Q, reset

  // Notes on the sheet:
  //   Synchronous Down Counter from 3 to 0 with reset
endmodule

module FSM (
  input  en,
  input  Next_State,
  output G,
  output Y,
  output R,
  output rst
);

  wire [1:0] multiplexer_1_out, register_2_q;

  Register #(.width(2)) register_1 ();  // open: D, en, Q, clk, clr
  Multiplexer #(.select(3), .width(2)) multiplexer_1 (
    .in0(2'b00), .in1(2'b01), .in2(2'b10), .in4(2'b01), .in5(2'b10), .in6(2'b00), .out(multiplexer_1_out),
    .sel({en, register_2_q}));  // open: in3, in7
  // Probe on multiplexer_1_out
  Register #(.width(2)) register_2 (.D(multiplexer_1_out), .Q(register_2_q), .clk(Next_State));  // open: en, clr
  // Probe on register_2_q
  and and_1 (G, register_2_q[0], ~register_2_q[1]);  // AND_Gate
  and and_2 (Y, ~register_2_q[0], register_2_q[1]);  // AND_Gate
  and and_3 (R, ~register_2_q[0], ~register_2_q[1]);  // AND_Gate

  assign rst = Next_State;
endmodule

module DownCounter_10 (
  input  en,
  input  clk,
  output [3:0] count
);

  wire and_1_out, and_2_out, and_3_out, and_4_out, t_ff_1_q, t_ff_2_q, t_ff_3_q;

  T_Flip_Flop t_ff_1 (.T(en), .clk(clk), .Q(t_ff_1_q), .Qn(count[0]), .preset(and_1_out));  // open: reset
  and and_1 (and_1_out, count[0], count[1], count[2], count[3]);
  and and_2 (and_2_out, en, t_ff_1_q);
  T_Flip_Flop t_ff_2 (.T(and_2_out), .clk(clk), .Q(t_ff_2_q), .Qn(count[1]));  // open: reset, preset
  and and_3 (and_3_out, and_2_out, t_ff_2_q);
  T_Flip_Flop t_ff_3 (.T(and_3_out), .clk(clk), .Q(t_ff_3_q), .Qn(count[2]), .preset(and_1_out));  // open: reset
  and and_4 (and_4_out, and_3_out, t_ff_3_q);
  T_Flip_Flop t_ff_4 (.T(and_4_out), .clk(clk), .Qn(count[3]));  // open: Q, reset, preset
endmodule

module main2 (
  input  in_1,
  input  en,
  input  stopper,
  input  in_4,
  output [3:0] out_5
);

  wire and_1_out, and_2_out, and_3_out, clk, fsm_1_g, fsm_1_r, fsm_1_y, G2, GA, not_1_out, nstate, or_1_out,
       pedestrian_button_1_en, pedestrian_button_1_stopped, R2, RA, Y2, YA;
  wire [3:0] downcounter_10_1_count, undriven;
  wire [7:0] bin2hex_1_hex0, bin2hex_1_hex1, HEX0, HEX1;

  and and_1 (and_1_out, ~out_5[0], ~out_5[1], ~out_5[2], ~out_5[3]);  // AND_Gate
  Clock u_clk (.out(clk));
  _7_Segment_Display #(.active("false")) u_7_segment_display_1 (
    .g(HEX1[6]), .f(HEX1[5]), .a(HEX1[0]), .b(HEX1[1]), .e(HEX1[4]), .d(HEX1[3]), .c(HEX1[2]), .dp(HEX1[7]));
  and and_2 (and_2_out, en, and_1_out);
  or or_1 (or_1_out, nstate, pedestrian_button_1_en);
  not not_1 (not_1_out, in_1);
  _7_Segment_Display #(.active("false")) u_7_segment_display_2 (
    .g(HEX0[6]), .f(HEX0[5]), .a(HEX0[0]), .b(HEX0[1]), .e(HEX0[4]), .d(HEX0[3]), .c(HEX0[2]), .dp(HEX0[7]));
  and and_3 (and_3_out, RA, R2);
  FSM fsm_1 (.en(en), .Next_State(and_2_out), .G(fsm_1_g), .Y(fsm_1_y), .R(fsm_1_r), .rst(nstate));
  countdown countdown_1 (.en_3(in_1), .clk(clk), .en_10(not_1_out), .HEX1(HEX1), .HEX0(HEX0), .count(out_5));
  pedestrian_button pedestrian_button_1 (
    .counter(undriven), .stopper(stopper), .reds(and_3_out), .done(in_4), .en(pedestrian_button_1_en),
    .stopped(pedestrian_button_1_stopped));
  // RGBLED rgbled_1: pin names not known; wires that end beside it: GA
  // RGBLED rgbled_2: pin names not known; wires that end beside it: YA, YA
  // RGBLED rgbled_3: pin names not known; wires that end beside it: RA
  switcher switcher_1 (.R(fsm_1_r), .Y(fsm_1_y), .G(fsm_1_g), .RA(RA), .YA(YA), .GA(GA), .RB(R2), .YB(Y2), .GB(G2));
  // RGBLED rgbled_4: pin names not known; wires that end beside it: G2
  // RGBLED rgbled_5: pin names not known; wires that end beside it: Y2, Y2
  // RGBLED rgbled_6: pin names not known; wires that end beside it: R2
  DownCounter_10 downcounter_10_1 (.clk(clk), .count(downcounter_10_1_count));  // open: en
  Bin2Hex bin2hex_1 (
    .v3(downcounter_10_1_count[3]), .v2(downcounter_10_1_count[2]), .v1(downcounter_10_1_count[1]),
    .v0(downcounter_10_1_count[0]), .HEX1(bin2hex_1_hex1), .HEX0(bin2hex_1_hex0));

  // Notes on the sheet:
  //   Counter Display
  //   Traffic Light A
  //   Traffic Light B
endmodule

module switcher (
  input  R,
  input  Y,
  input  G,
  output RA,
  output YA,
  output GA,
  output RB,
  output YB,
  output GB
);

  wire and_1_out, and_4_out, d_ff_1_qn;

  D_Flip_Flop #(.trigger("falling")) d_ff_1 (.D(d_ff_1_qn), .clk(R), .Qn(d_ff_1_qn));  // open: Q, preset, reset
  and and_1 (and_1_out, d_ff_1_qn, R);
  and and_2 (YA, Y, d_ff_1_qn);
  and and_3 (GA, d_ff_1_qn, G);
  and and_4 (and_4_out, ~d_ff_1_qn, R);  // AND_Gate
  and and_5 (YB, ~d_ff_1_qn, Y);  // AND_Gate
  and and_6 (GB, ~d_ff_1_qn, G);  // AND_Gate
  or or_1 (RA, ~d_ff_1_qn, and_1_out);  // OR_Gate
  or or_2 (RB, d_ff_1_qn, and_4_out);
endmodule

module countdown (
  input  en_3,
  input  clk,
  input  en_10,
  output [7:0] HEX1,
  output [7:0] HEX0,
  output [3:0] count
);

  wire [3:0] downcounter_3_1_count, downcounter_10_1_count;
  wire [7:0] bin2hex_1_hex0, bin2hex_1_hex1, bin2hex_2_hex0, bin2hex_2_hex1;

  DownCounter_3 downcounter_3_1 (.en(en_3), .clk(clk), .count(downcounter_3_1_count));
  DownCounter_10 downcounter_10_1 (.en(en_10), .clk(clk), .count(downcounter_10_1_count));
  Multiplexer #(.select(2), .width(4)) multiplexer_1 (
    .in0(downcounter_10_1_count), .in1(downcounter_3_1_count), .in2(downcounter_10_1_count),
    .in3(downcounter_3_1_count), .out(count), .sel({clk, en_3}));
  Bin2Hex bin2hex_1 (
    .v3(downcounter_3_1_count[3]), .v2(downcounter_3_1_count[2]), .v1(downcounter_3_1_count[1]),
    .v0(downcounter_3_1_count[0]), .HEX1(bin2hex_1_hex1), .HEX0(bin2hex_1_hex0));
  Bin2Hex bin2hex_2 (
    .v3(downcounter_10_1_count[3]), .v2(downcounter_10_1_count[2]), .v1(downcounter_10_1_count[1]),
    .v0(downcounter_10_1_count[0]), .HEX1(bin2hex_2_hex1), .HEX0(bin2hex_2_hex0));
  Multiplexer #(.width(8)) multiplexer_2 (.in0(bin2hex_2_hex1), .in1(bin2hex_1_hex1), .out(HEX1), .sel(en_3));
  Multiplexer #(.width(8)) multiplexer_3 (.in0(bin2hex_2_hex0), .in1(bin2hex_1_hex0), .out(HEX0), .sel(en_3));
endmodule
